# Fritzing sketch monaje_temperatura (saved by Fritzing 0.9.3b)
breadboards: 1

parts:
  Grove1 = Grove Temperature Sensor
  U2 = NodeMCU V3.0

nets:
  GND: Grove1.GND, U2.GND
  VCC: Grove1.VCC, U2.3V3
  N1: Grove1.SIG, U2.A0

custom parts:
  NodeMCU V3.0: NodeMcu V3 Lua WIFI Development Board
